# Fritzing sketch led-matrix-bb (saved by Fritzing 1.0.6)
breadboards: 2

parts:
  Part1 = Arduino Uno (Rev3)
  R1 = Resistor [tolerance=±5% power=0.25W resistance=1000 package=THT]
  R2 = Resistor [tolerance=±5% power=0.25W resistance=1000 package=THT]
  R3 = Resistor [tolerance=±5% power=0.25W resistance=1000 package=THT]
  R4 = Resistor [tolerance=±5% power=0.25W resistance=1000 package=THT]
  R5 = Resistor [tolerance=±5% power=0.25W resistance=1000 package=THT]
  R6 = Resistor [tolerance=±5% power=0.25W resistance=1000 package=THT]
  R7 = Resistor [tolerance=±5% power=0.25W resistance=1000 package=THT]
  R8 = Resistor [tolerance=±5% power=0.25W resistance=1000 package=THT]
  Disp1 = 60mm 8x8 dot matrix row cathode led display with narrow pcb pads

nets:
  N1: Part1.A0, R1.Pin_0
  N2: Part1.A1, R2.Pin_0
  N3: Part1.A2, R3.Pin_0
  N4: Part1.A3, R4.Pin_0
  N5: Part1.D8, Disp1.pin_11
  N6: Part1.D9_PWM, Disp1.pin_6
  N7: Part1.D10_PWM/SS, Disp1.pin_10
  N8: Part1.D11_PWM/MOSI, Disp1.pin_5
  N9: Part1.D12/MISO, Disp1.pin_4
  N10: Part1.D13/SCK, Disp1.pin_13
  N11: Part1.D2, R6.Pin_0
  N12: Part1.D3_PWM, R5.Pin_0
  N13: Part1.D4, R7.Pin_0
  N14: Part1.D5_PWM, R8.Pin_0
  N15: Part1.D6_PWM, Disp1.pin_16
  N16: Part1.D7, Disp1.pin_15
  N17: R1.Pin_1, Disp1.pin_9
  N18: R2.Pin_1, Disp1.pin_14
  N19: R4.Pin_1, Disp1.pin_12
  N20: R5.Pin_1, Disp1.pin_7
  N21: R6.Pin_1, Disp1.pin_1
  N22: R7.Pin_1, Disp1.pin_2
  N23: R8.Pin_1, Disp1.pin_3

notes:
  rijen 1 - 8
  kolommen 1 - 8
  pin 1
  pin 8
  pin 16
  pin 9
